// Logisim project Adder-Lib.circ as structural Verilog: 6 circuits, main circuit main
module main (
  input  Decider,
  input  A2,
  input  A1,
  input  A0,
  input  B2,
  input  B1,
  input  B0,
  output S,
  output R3,
  output R2,
  output R1,
  output R0
);

  wire controlled_4bits_add_sub_1_r___bit_0, controlled_4bits_add_sub_1_r___bit_1,
       controlled_4bits_add_sub_1_r___bit_2, controlled_4bits_add_sub_1_r___bit_4, s_2s_1_a0, s_2s_1_a1,
       s_2s_1_a2, s_2s_1_s, s_2s_2_a0, s_2s_2_a1, s_2s_2_a2, s_2s_2_s;

  s__2s s_2s_1 (.I0(A0), .I1(A1), .I2(A2), .A0(s_2s_1_a0), .A1(s_2s_1_a1), .A2(s_2s_1_a2), .S(s_2s_1_s));
  s__2s s_2s_2 (.I0(B0), .I1(B1), .I2(B2), .A0(s_2s_2_a0), .A1(s_2s_2_a1), .A2(s_2s_2_a2), .S(s_2s_2_s));
  Controlled_4bits_Add_sub controlled_4bits_add_sub_1 (
    .A___Bit_3(s_2s_1_s), .A___Bit_2(s_2s_1_a2), .A___Bit_1(s_2s_1_a1), .A___Bit_0(s_2s_1_a0),
    .B___Bit_3(s_2s_2_s), .B___Bit_2(s_2s_2_a2), .B___Bit_1(s_2s_2_a1), .B___Bit_0(s_2s_2_a0),
    .Decider(Decider), .R___Bit_0(controlled_4bits_add_sub_1_r___bit_0),
    .R___Bit_1(controlled_4bits_add_sub_1_r___bit_1), .R___Bit_2(controlled_4bits_add_sub_1_r___bit_2),
    .R___Bit_3(S), .R___Bit_4(controlled_4bits_add_sub_1_r___bit_4));
  _2s__s u_2s_s_1 (
    .S(S), .I2(controlled_4bits_add_sub_1_r___bit_2), .I1(controlled_4bits_add_sub_1_r___bit_1),
    .I0(controlled_4bits_add_sub_1_r___bit_0), .A2(R2), .A1(R1), .A0(R0));

  assign R3 = 1'b0;

  // Notes on the sheet:
  //   Signed to 2s comp
  //   Signed to 2s comp
  //   4 Bits full adder
  //   2s comp to 3 bits signed
  //   Made By: Mohamed Ahmed Abdelhamid
  //   Github ---> MohamedAbdelhamid0
endmodule

module Half_adder (
  input  Inp1,
  input  Inp2,
  output Result,
  output Carry_out
);

  xor xor_1 (Result, Inp1, Inp2);
  and and_1 (Carry_out, Inp1, Inp2);

  // Notes on the sheet:
  //   Made By: Mohamed Ahmed Abdelhamid
  //   Github ---> MohamedAbdelhamid0
endmodule

module Full_adder (
  input  Cin,
  input  Inp1,
  input  Inp2,
  output Output,
  output Carry_out
);

  wire and_1_out, and_2_out, or_1_out;

  xor xor_1 (Output, Cin, Inp1, Inp2);
  and and_1 (and_1_out, Inp1, Inp2);
  or or_1 (or_1_out, Inp1, Inp2);
  and and_2 (and_2_out, Cin, or_1_out);
  or or_2 (Carry_out, and_1_out, and_2_out);

  // Notes on the sheet:
  //   Made By: Mohamed Ahmed Abdelhamid
  //   Github ---> MohamedAbdelhamid0
endmodule

module s__2s (
  input  I0,
  input  I1,
  input  I2,
  output A0,
  output A1,
  output A2,
  output S
);

  wire and_1_out, and_2_out, and_3_out, and_4_out, and_5_out, and_6_out, and_7_out, not_1_out, not_2_out,
       not_3_out;

  not not_1 (not_1_out, I2);
  not not_2 (not_2_out, I0);
  not not_3 (not_3_out, I1);
  and and_1 (and_1_out, I2, I0);
  and and_2 (and_2_out, I2, I1);
  and and_3 (and_3_out, I2, I0);
  and and_4 (and_4_out, I2, I1);
  and and_5 (and_5_out, not_1_out, I1);
  and and_6 (and_6_out, I1, not_2_out);
  and and_7 (and_7_out, I2, not_3_out, I0);
  or or_1 (A2, and_1_out, and_2_out);
  or or_2 (S, and_3_out, and_4_out);
  or or_3 (A1, and_5_out, and_6_out, and_7_out);

  assign A0 = I0;

  // Notes on the sheet:
  //   Made By: Mohamed Ahmed Abdelhamid
  //   Github ---> MohamedAbdelhamid0
endmodule

module _2s__s (
  input  S,
  input  I2,
  input  I1,
  input  I0,
  output A2,
  output A1,
  output A0
);

  wire and_1_out, and_2_out, and_3_out, and_4_out, and_5_out, and_6_out, and_7_out, not_1_out, not_2_out,
       not_3_out, not_4_out, not_5_out, not_6_out, not_7_out, not_8_out;

  not not_1 (not_1_out, S);
  and and_1 (and_1_out, not_1_out, I2);
  not not_2 (not_2_out, I1);
  and and_2 (and_2_out, I2, not_2_out, not_3_out);
  not not_3 (not_3_out, I0);
  and and_3 (and_3_out, S, not_4_out, I0);
  not not_4 (not_4_out, I2);
  not not_5 (not_5_out, I2);
  and and_4 (and_4_out, S, not_5_out, I1);
  not not_6 (not_6_out, S);
  and and_5 (and_5_out, not_6_out, I1);
  and and_6 (and_6_out, I1, not_7_out);
  not not_7 (not_7_out, I0);
  not not_8 (not_8_out, I1);
  and and_7 (and_7_out, S, not_8_out, I0);
  or or_1 (A2, and_1_out, and_2_out, and_3_out, and_4_out);
  or or_2 (A1, and_5_out, and_6_out, and_7_out);

  assign A0 = I0;

  // Notes on the sheet:
  //   Made By: Mohamed Ahmed Abdelhamid
  //   Github ---> MohamedAbdelhamid0
endmodule

module Controlled_4bits_Add_sub (
  input  A___Bit_3,
  input  A___Bit_2,
  input  A___Bit_1,
  input  A___Bit_0,
  input  B___Bit_3,
  input  B___Bit_2,
  input  B___Bit_1,
  input  B___Bit_0,
  input  Decider,
  output R___Bit_0,
  output R___Bit_1,
  output R___Bit_2,
  output R___Bit_3,
  output R___Bit_4
);

  wire full_adder_1_carry_out, full_adder_2_carry_out, full_adder_3_carry_out, xor_1_out, xor_2_out,
       xor_3_out, xor_4_out;

  xor xor_1 (xor_1_out, B___Bit_0, Decider);
  xor xor_2 (xor_2_out, B___Bit_1, Decider);
  xor xor_3 (xor_3_out, B___Bit_2, Decider);
  xor xor_4 (xor_4_out, B___Bit_3, Decider);
  Full_adder full_adder_1 (
    .Cin(Decider), .Inp1(A___Bit_0), .Inp2(xor_1_out), .Output(R___Bit_0), .Carry_out(full_adder_1_carry_out));
  Full_adder full_adder_2 (
    .Cin(full_adder_1_carry_out), .Inp1(A___Bit_1), .Inp2(xor_2_out), .Output(R___Bit_1),
    .Carry_out(full_adder_2_carry_out));
  Full_adder full_adder_3 (
    .Cin(full_adder_2_carry_out), .Inp1(A___Bit_2), .Inp2(xor_3_out), .Output(R___Bit_2),
    .Carry_out(full_adder_3_carry_out));
  Full_adder full_adder_4 (
    .Cin(full_adder_3_carry_out), .Inp1(A___Bit_3), .Inp2(xor_4_out), .Output(R___Bit_3),
    .Carry_out(R___Bit_4));

  // Notes on the sheet:
  //   Made By: Mohamed Ahmed Abdelhamid
  //   Github ---> MohamedAbdelhamid0
endmodule
