// Logisim project Full.circ as structural Verilog: 1 circuit, main circuit main
module main (
  input  [1:0] Selector_of_Operation,
  input  Sub_Add_switch,
  input  in_3,
  input  in_4,
  input  in_5,
  input  in_6,
  input  B_Inputs,
  input  in_8
);

  wire main_1_r0, main_1_r1, main_1_r2, main_1_r3, main_1_s, main_2_r0, main_2_r1, main_2_r2, main_2_r3,
       main_2_s, main_3__0, main_3__1, main_3__2, main_3__3, multiplexer_1_out, multiplexer_2_out,
       multiplexer_3_out, multiplexer_4_out, multiplexer_5_out, n7_segment_display_driver_1_p5,
       n7_segment_display_driver_1_p6, n7_segment_display_driver_1_p7, n7_segment_display_driver_1_p8,
       n7_segment_display_driver_1_p9, n7_segment_display_driver_1_p10, n7_segment_display_driver_1_p11;

  Adder_Lib_main main_1 (
    .A2(in_3), .A1(in_4), .A0(in_5), .B2(in_6), .B1(B_Inputs), .B0(in_8), .Decider(Sub_Add_switch),
    .S(main_1_s), .R3(main_1_r3), .R2(main_1_r2), .R1(main_1_r1), .R0(main_1_r0));
  Multiply_Lib_main main_2 (
    .A2(in_3), .A1(in_4), .A0(in_5), .B2(in_6), .B1(B_Inputs), .B0(in_8), .S(main_2_s), .R3(main_2_r3),
    .R2(main_2_r2), .R1(main_2_r1), .R0(main_2_r0));
  Increment_A_main main_3 (
    .A0(in_5), .A1(in_4), .A2(in_3), ._0(main_3__0), ._1(main_3__1), ._2(main_3__2), ._3(main_3__3));
  Multiplexer #(.select(2)) multiplexer_1 (
    .in0(main_1_s), .in1(main_2_s), .in2(1'b0), .in3(1'b0), .out(multiplexer_1_out),
    .sel(Selector_of_Operation));  // open: en
  Multiplexer #(.select(2)) multiplexer_2 (
    .in0(main_1_r3), .in1(main_2_r3), .in2(main_3__3), .in3(1'b0), .out(multiplexer_2_out),
    .sel(Selector_of_Operation));  // open: en
  Multiplexer #(.select(2)) multiplexer_3 (
    .in0(main_1_r2), .in1(main_2_r2), .in2(main_3__2), .in3(1'b0), .out(multiplexer_3_out),
    .sel(Selector_of_Operation));  // open: en
  Multiplexer #(.select(2)) multiplexer_4 (
    .in0(main_1_r1), .in1(main_2_r1), .in2(main_3__1), .in3(1'b0), .out(multiplexer_4_out),
    .sel(Selector_of_Operation));  // open: en
  Multiplexer #(.select(2)) multiplexer_5 (
    .in0(main_1_r0), .in1(main_2_r0), .in2(main_3__0), .in3(1'b0), .out(multiplexer_5_out),
    .sel(Selector_of_Operation));  // open: en
  // _7_segment_display_driver 7_segment_display_driver_1: pin names not known; wires that end beside it: multiplexer_2_out, multiplexer_3_out, multiplexer_4_out, multiplexer_5_out, n7_segment_display_driver_1_p5, n7_segment_display_driver_1_p6, n7_segment_display_driver_1_p7, n7_segment_display_driver_1_p8, n7_segment_display_driver_1_p9, n7_segment_display_driver_1_p10, n7_segment_display_driver_1_p11
  _7_Segment_Display u_7_segment_display_1 (.g(multiplexer_1_out));  // open: f, a, b, e, d, c, dp
  _7_Segment_Display u_7_segment_display_2 (
    .g(n7_segment_display_driver_1_p11), .f(n7_segment_display_driver_1_p10),
    .a(n7_segment_display_driver_1_p5), .b(n7_segment_display_driver_1_p6),
    .e(n7_segment_display_driver_1_p9), .d(n7_segment_display_driver_1_p8), .c(n7_segment_display_driver_1_p7));  // open: dp

  // Notes on the sheet:
  //   A Inputs
  //   Increment A (10)
  //   ADD/SUB (00)
  //   MULTIPLY (01)
  //   Made by Mohamed Ahmed Abdelhamid
  //   GIthub ---> MohamedAbdelhamid0
endmodule
