// Logisim project Increment A.circ as structural Verilog: 1 circuit, main circuit main
module main (
  input  A0,
  input  A1,
  input  A2,
  output _0,
  output _1,
  output _2,
  output _3
);

  wire half_adder_1_carry_out, half_adder_2_carry_out;

  Half_adder half_adder_1 (.Inp1(1'b1), .Inp2(A0), .Result(_0), .Carry_out(half_adder_1_carry_out));
  Half_adder half_adder_2 (.Inp1(half_adder_1_carry_out), .Inp2(A1), .Result(_1), .Carry_out(half_adder_2_carry_out));
  Half_adder half_adder_3 (.Inp1(half_adder_2_carry_out), .Inp2(A2), .Result(_2), .Carry_out(_3));
endmodule
