// Logisim project Multiply-Lib.circ as structural Verilog: 4 circuits, main circuit main
module main (
  input  A2,
  input  A1,
  input  A0,
  input  B2,
  input  B1,
  input  B0,
  output S,
  output R3,
  output R2,
  output R1,
  output R0
);

  _2_bits_multiplier u_2_bits_multiplier_1 (.B0(B0), .B1(B1), .A0(A0), .A1(A1), .R3(R3), .R2(R2), .R1(R1), .R0(R0));
  Sign_output sign_output_1 (.As(A2), .Bs(B2), .I0(R0), .I1(R1), .I2(R2), .I3(R3), .SIGN(S));

  // Notes on the sheet:
  //   Made By: Mohamed Ahmed Abdelhamid
  //   Github ---> MohamedAbdelhamid0
endmodule

module Half_adder (
  input  Inp1,
  input  Inp2,
  output Result,
  output Carry_out
);

  xor xor_1 (Result, Inp1, Inp2);
  and and_1 (Carry_out, Inp1, Inp2);

  // Notes on the sheet:
  //   Made By: Mohamed Ahmed Abdelhamid
  //   Github ---> MohamedAbdelhamid0
endmodule

module _2_bits_multiplier (
  input  B0,
  input  B1,
  input  A0,
  input  A1,
  output R3,
  output R2,
  output R1,
  output R0
);

  wire and_2_out, and_3_out, and_4_out, half_adder_1_carry_out;

  and and_1 (R0, B0, A0);
  and and_2 (and_2_out, A1, B0);
  and and_3 (and_3_out, A0, B1);
  and and_4 (and_4_out, A1, B1);
  Half_adder half_adder_1 (.Inp1(and_2_out), .Inp2(and_3_out), .Result(R1), .Carry_out(half_adder_1_carry_out));
  Half_adder half_adder_2 (.Inp1(half_adder_1_carry_out), .Inp2(and_4_out), .Result(R2), .Carry_out(R3));

  // Notes on the sheet:
  //   Made By: Mohamed Ahmed Abdelhamid
  //   Github ---> MohamedAbdelhamid0
endmodule

module Sign_output (
  input  As,
  input  Bs,
  input  I0,
  input  I1,
  input  I2,
  input  I3,
  output SIGN
);

  wire or_1_out, xor_1_out;

  xor xor_1 (xor_1_out, As, Bs);
  or or_1 (or_1_out, I0, I1, I2, I3);
  and and_1 (SIGN, xor_1_out, or_1_out);

  // Notes on the sheet:
  //   Made By: Mohamed Ahmed Abdelhamid
  //   Github ---> MohamedAbdelhamid0
endmodule
